// Logisim project a-simulation.circ as structural Verilog
module A_Sim (
  input  in_1,
  input  in_2,
  input  in_3,
  output out
);

  wire and_1_out, and_2_out, clock_1_out, not_1_out, not_2_out, not_3_out;
  wire [2:0] counter_1_q;

  Clock clock_1 (.out(clock_1_out));
  Counter #(.width(3), .max('h7)) counter_1 (
    .load(in_1), .count(in_2), .Q(counter_1_q), .clk(clock_1_out), .clr(in_3));  // open: D, carry
  not not_1 (not_1_out, counter_1_q[1]);
  and and_1 (and_1_out, not_1_out, not_2_out);
  not not_2 (not_2_out, counter_1_q[2]);
  not not_3 (not_3_out, counter_1_q[0]);
  and and_2 (and_2_out, not_3_out, counter_1_q[1]);
  or or_1 (out, and_1_out, and_2_out);

  // Notes on the sheet:
  //   Morse "A" blinky
endmodule
