// Logisim project ian-simulation.circ as structural Verilog
module IAN (
  input  in_1,
  input  in_2,
  input  in_3,
  output out
);

  wire and_1_out, and_2_out, and_3_out, and_4_out, clock_1_out, not_1_out, not_2_out, not_3_out, not_4_out,
       not_5_out, not_6_out, not_7_out, not_8_out, not_9_out;
  wire [4:0] counter_1_q;

  Counter #(.width(5), .max('h1f)) counter_1 (
    .load(in_1), .count(in_2), .Q(counter_1_q), .clk(clock_1_out), .clr(in_3));  // open: D, carry
  Clock clock_1 (.out(clock_1_out));
  not not_1 (not_1_out, counter_1_q[3]);
  not not_2 (not_2_out, counter_1_q[2]);
  not not_3 (not_3_out, counter_1_q[0]);
  not not_4 (not_4_out, counter_1_q[4]);
  not not_5 (not_5_out, counter_1_q[0]);
  not not_6 (not_6_out, counter_1_q[4]);
  not not_7 (not_7_out, counter_1_q[2]);
  not not_8 (not_8_out, counter_1_q[1]);
  not not_9 (not_9_out, counter_1_q[4]);
  and and_1 (and_1_out, not_1_out, not_2_out, not_3_out);
  and and_2 (and_2_out, not_4_out, counter_1_q[1], not_5_out);
  and and_3 (and_3_out, not_6_out, counter_1_q[3], not_7_out, not_8_out);
  and and_4 (and_4_out, not_9_out, counter_1_q[3], counter_1_q[2], counter_1_q[1]);
  or or_1 (out, and_1_out, and_2_out, and_3_out, and_4_out);
endmodule
